// Logisim project CPU.circ as structural Verilog
module ALU (
  input  [3:0] A,
  input  [3:0] B,
  input  [3:0] OP,
  input  [1:0] K,
  input  CF,
  output [3:0] Y,
  output [3:0] HIN,
  output Z,
  output C,
  output N,
  output V,
  output DIVZ
);

  wire and_1_out, and_2_out, CADD, CIN, D1, D2, D3, D4, D14, SC, SUBM, VADD, xnor_1_out, xor_3_out;
  wire [3:0] BP, S, SUBM4;

  and and_1 (and_1_out, D1, CF);
  and and_2 (and_2_out, D3, ~CF);  // AND_Gate
  or or_1 (SUBM, D2, D3, D14);
  // Probe on SC
  xor xor_1 (CADD, SUBM, SC);
  assign SUBM4 = {{3{SUBM}}, SUBM};  // Bit_Extender bit_extender_1
  Decoder #(.enable("false"), .select(4)) decoder_1 (
    .out1(D1), .out2(D2), .out3(D3), .out4(D4), .out14(D14), .sel(OP));  // open: out0, out5, out6, out7, out8, out9, out10, out11, out12, out13, out15
  assign BP = B ^ SUBM4;  // XOR_Gate xor_2, 4 bits wide
  Adder #(.width(4)) adder_1 (.a(A), .b(BP), .out(S), .cin(CIN), .cout(SC));
  // Probe on CADD
  xor xor_3 (xor_3_out, A[3], S[3]);
  or or_2 (CIN, and_1_out, and_2_out, D2, D14);
  // Probe on S
  xnor xnor_1 (xnor_1_out, A[3], BP[3]);
  and and_3 (VADD, xnor_1_out, xor_3_out);
  // Probe on VADD
endmodule
